# Fritzing sketch tuxdroid (saved by Fritzing 0.9.3b)
stripboards: 6
breadboards: 1

parts:
  U1 = L9110 H-bridge module [part_number="L9110 H-bridge"]
  Raspberry_Pi_1 = Raspberry Pi 3 [part_number=RPI-3-V1.2]  # not connected
  Part1 = Adafruit T-Cobbler Plus [part_number="Adafruit #1989 and #2028"]

nets:
  GND: U1.GND, Part1.GND
  VCC: U1.VCC, Part1.+5V

notes:
  - Y/W
  Left wings
  button
  - O/B
  Right wings
  button
  - R/B
  Wings move
  sensor
  * R/W
  IR Receiver
  * Black
  Groud for led
  * Blue
  IR Transmetter
  * G
  Left eye Led
  * Y
  Right eye Led
  * O
  Light sensor
  * Gy/Br
  head button
  * R/W
  Eyes open
  sensor
  * O/B
  Eyes close
  sensor
  * Y/G
  Mouth open
  sensor
  * G/B
  Mouth close
  sensor
  * B/R
  Microphone
  * R/W
  Eyes/Mouth Motor
  * B/R
  Wings Motor

custom parts:
  Adafruit T-Cobbler Plus: The Raspberry Pi has landed on the Maker World like a 40-GPIO pinned, quad-USB ported, credit card sized bomb of DIY joy. And while you can use most of our great Model B accessories by hooking up our downgrade cable, its probably a good time to upgrade your set up and accessorize using all of the 40 pins. That's why we now carry the Assembled Adafruit Pi T-Cobbler Plus - Breakout + Cable for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
